# Fritzing sketch CAD_drawing (saved by Fritzing 0.9.5d)
breadboards: 1

parts:
  Mod1 = Raspberry Pi 4B
  IC1 = Rasberry Pi NIOR Camera [chip_label=IC package="DIP (Dual Inline) [THT]"]  # not connected
  3mmレッドLED = smd LED [color="Red (635nm)" package="0805 [SMD]"]
  R1 = Resistor [tolerance=±5% resistance=47 package="0805 [SMD]"]
  NchパワーMOSFET = MOSFET-NCHANNEL [part_number="60V25A 2SK2232\n" package=to220v]
  R3 = Resistor [tolerance=±5% resistance=47 package="0603 [SMD]"]
  R2 = Resistor [tolerance=±5% resistance=47 package="0805 [SMD]"]
  R6 = Resistor [tolerance=±5% resistance=10k package="0805 [SMD]"]
  NchパワーMOSFET1 = MOSFET-NCHANNEL [part_number="60V25A 2SK2232\n" package=to220v]
  R7 = Resistor [tolerance=±5% resistance=10k package="0805 [SMD]"]
  S2 = Momentary Switch [package=ksa_sealed_tac_switch]
  R5 = Resistor [tolerance=±5% resistance=10 package="0805 [SMD]"]
  U1 = SWITCH_SPDT [package=kps-1290]
  5mm赤外線LED = smd LED [color="Infrared (940nm)" part_number=OSI5LA5A33A-B package="0805 [SMD]"]
  5mm赤外線LED_2 = smd LED [color="Infrared (940nm)" part_number=OSI5LA5A33A-B package="0805 [SMD]"]
  5mm赤外線LED_3 = smd LED [color="Infrared (940nm)" part_number=OSI5LA5A33A-B package="0805 [SMD]"]
  R4 = Resistor [tolerance=±5% resistance=100 package="0805 [SMD]"]
  赤外線リモコン受信モジュール = Infra red receiver [part_number="OSRB38C9AA\n"]

nets (from the schematic view):
  N1: Mod1.5V, U1.P
  N2: Mod1.GPIO18, NchパワーMOSFET1.G, R7.Pin_1
  N3: Mod1.GPIO24, 赤外線リモコン受信モジュール.Data
  GND: Mod1.GND, NchパワーMOSFET.S, R6.Pin_0, NchパワーMOSFET1.S, R7.Pin_0, 赤外線リモコン受信モジュール.GND
  N4: Mod1.GPIO8, NchパワーMOSFET.G, R6.Pin_1
  N5: 3mmレッドLED.cathode, NchパワーMOSFET1.D, S2.1, S2.2
  N6: 3mmレッドLED.anode, R5.Pin_1
  N7: R1.Pin_0, R3.Pin_0, R2.Pin_0, U1.O, R4.Pin_0
  N8: R1.Pin_1, 5mm赤外線LED_3.anode
  N9: NchパワーMOSFET.D, S2.3, S2.4, 5mm赤外線LED.cathode, 5mm赤外線LED_2.cathode, 5mm赤外線LED_3.cathode
  N10: R3.Pin_1, 5mm赤外線LED.anode
  N11: R2.Pin_1, 5mm赤外線LED_2.anode
  N12: R5.Pin_0, R4.Pin_1
  N13: U1.S, 赤外線リモコン受信モジュール.VCC

custom parts:
  Rasberry Pi NIOR Camera: Camera
  Momentary Switch: Momentary Switch Button commonly used for reset or general input. Spark Fun Electronics SKU : COM-00097
